// Logisim project processor_pipelined.circ as structural Verilog: 14 circuits, main circuit Processor
module Processor (
  input  Reset,
  output halt,
  output [31:0] out_3,
  output [31:0] out_4,
  output [31:0] out_5
);

  wire clock_1_out, comparator_1_eq, comparator_2_eq, comparator_3_eq, mainctrl_1_extsign, MemWrite,
       mudv_1_busy, not_1_out, RegWrite, sfwctrl_1_fw2, stallctrl_1_stall, undriven_2;
  wire [0:0] W_MCtrl_q;
  wire [1:0] dfwctrl_1_fw1, dfwctrl_1_fw2, E_MCtrl_q, E_tnew_q, E_WCtrl_q_2, M_MCtrl_q, M_tnew_q,
       M_WCtrl_q_2, mainctrl_1_dmwrstate, mainctrl_1_pcsrc, mainctrl_1_tninit, multiplexer_15_out,
       multiplexer_17_out, subtractor_2_out, subtractor_3_out, undriven, undriven_3, undriven_4, W_tnew_q;
  wire [2:0] E_WCtrl_q, efwctrl_1_fw1, efwctrl_1_fw2, M_WCtrl_q;
  wire [3:0] mainctrl_1_alufn;
  wire [4:0] E_rreg1_q, E_rreg2_q, E_shamt_q, E_wreg_q, fieldsel_1_rd, fieldsel_1_rs, fieldsel_1_rt,
       fieldsel_1_shamt, M_rreg2_q, M_wreg_q, mainctrl_1_grfwen, multiplexer_7_out, multiplexer_11_out,
       RegAddr;
  wire [4:1] W_WCtrl_q;
  wire [5:0] aluctrl_1_aluop, E_ECtrl_q, fieldsel_1_funct, fieldsel_1_opcode;
  wire [15:0] fieldsel_1_imm;
  wire [31:0] adder_1_out, adder_2_out, adder_3_out, alu_1_res, bit_extender_1_out, bit_extender_2_out,
       bit_extender_3_out, D_instr_q, D_npc_q, D_pc4_q, datamem_1_rdat, E_imm_q, E_npc_q, E_pc8_q, E_rd1_q,
       E_rd2_q, grf_1_rdat1, grf_1_rdat2, instrmem_1_instr, M_addr_q, M_DMwdat_q, M_pc8_q, MemAddr, MemData,
       mudv_1_hi, mudv_1_lo, multiplexer_1_out, multiplexer_4_out, multiplexer_5_out, multiplexer_6_out,
       multiplexer_8_out, multiplexer_9_out, multiplexer_10_out, multiplexer_12_out, multiplexer_13_out,
       multiplexer_14_out, multiplexer_16_out, npc, RegData, shifter_1_out, subtractor_1_out, W_dmrdat_q,
       W_pc8_q;
  wire [31:2] fieldsel_1_instr_ind;

  Clock clock_1 (.out(clock_1_out));
  Multiplexer #(.select(2), .width(32), .enable("false")) multiplexer_1 (
    .in0(adder_1_out), .in1(multiplexer_6_out), .in2({fieldsel_1_instr_ind, 2'b00}), .in3(multiplexer_8_out),
    .out(multiplexer_1_out), .sel(mainctrl_1_pcsrc));
  // Probe on multiplexer_1_out
  PC pc_1 (.npc(multiplexer_1_out), .pc(out_5), .RST(Reset), .CLK(clock_1_out), .pcen(not_1_out));
  Counter #(.width(32), .max('h4), .ongoal("stay")) counter_1 (
    .carry(halt), .clk(clock_1_out));  // open: load, D, count, Q, clr
  Adder #(.width(32)) adder_1 (.a(out_5), .b(32'h4), .out(adder_1_out));  // open: cin, cout
  // Probe on out_5
  InstrMem instrmem_1 (.pc(out_5), .instr(instrmem_1_instr));
  assign bit_extender_1_out = {{27{1'b0}}, RegAddr};  // Bit_Extender bit_extender_1
  Multiplexer #(.select(2), .width(32), .enable("false")) multiplexer_2 (
    .in0(npc), .in1(MemData), .in2(RegData), .out(out_4), .sel({RegWrite, MemWrite}));  // open: in3
  // Probe on instrmem_1_instr
  // Probe on out_3
  Pull_Resistor pull_resistor_1 (.node(out_3));
  Multiplexer #(.select(2), .width(32), .enable("false")) multiplexer_3 (
    .in0({32{1'b0}}), .in1(MemAddr), .in2(bit_extender_1_out), .out(out_3), .sel({RegWrite, MemWrite}));  // open: in3
  // Probe on out_4
  Pull_Resistor pull_resistor_2 (.node(out_4));
  // Probe on out_5
  Register #(.width(32)) D_pc4 (.D(adder_1_out), .en(not_1_out), .Q(D_pc4_q), .clk(clock_1_out), .clr(Reset));
  // Probe on D_pc4_q
  // Probe on D_npc_q
  Register #(.width(32)) D_npc (.D(multiplexer_1_out), .Q(D_npc_q), .clk(clock_1_out), .clr(Reset));  // open: en
  // Probe on D_instr_q
  Register #(.width(32)) D_instr (.D(instrmem_1_instr), .en(not_1_out), .Q(D_instr_q), .clk(clock_1_out), .clr(Reset));
  not not_1 (not_1_out, stallctrl_1_stall);
  Multiplexer #(.width(32), .enable("false")) multiplexer_4 (
    .in0(D_instr_q), .in1({32{1'b0}}), .out(multiplexer_4_out), .sel(stallctrl_1_stall));
  // Probe on multiplexer_4_out
  StallCtrl stallctrl_1 (
    .Ewreg(E_wreg_q), .Mwreg(M_wreg_q), .Etnew(E_tnew_q), .Mtnew(M_tnew_q), .stall(stallctrl_1_stall),
    .Drs(D_instr_q[25:21]), .Drt(D_instr_q[20:16]), .EGRFwen(E_WCtrl_q[0]), .MGRFwen(M_WCtrl_q[0]),
    .opcode(D_instr_q[31:26]), .funct(D_instr_q[5:0]));
  Subtractor #(.width(32)) subtractor_1 (.a(D_pc4_q), .b(32'h4), .out(subtractor_1_out));  // open: bin, bout
  FieldSel fieldsel_1 (
    .instr(multiplexer_4_out), .shamt(fieldsel_1_shamt), .rs(fieldsel_1_rs), .rt(fieldsel_1_rt),
    .rd(fieldsel_1_rd), .imm(fieldsel_1_imm), .opcode(fieldsel_1_opcode), .funct(fieldsel_1_funct),
    .instr_ind(fieldsel_1_instr_ind[27:2]));
  // Probe on fieldsel_1_rs
  // Probe on fieldsel_1_rt
  MainCtrl mainctrl_1 (
    .opcode(fieldsel_1_opcode), .GRFwen(mainctrl_1_grfwen[0]), .GRFwdst(mainctrl_1_grfwen[4:3]),
    .GRFwdatsrc(mainctrl_1_grfwen[2:1]), .ALUfn(mainctrl_1_alufn), .ALUshsrc(aluctrl_1_aluop[4]),
    .ALUien(aluctrl_1_aluop[5]), .EXTsign(mainctrl_1_extsign), .DMwrstate(mainctrl_1_dmwrstate),
    .funct(fieldsel_1_funct), .PCsrc(mainctrl_1_pcsrc), .TNinit(mainctrl_1_tninit));
  Adder #(.width(32)) adder_2 (.a(D_pc4_q), .b(32'h4), .out(adder_2_out));  // open: cin, cout
  assign bit_extender_2_out = {{16{1'b0}}, fieldsel_1_imm};  // Bit_Extender bit_extender_2
  assign bit_extender_3_out = {{16{fieldsel_1_imm[15]}}, fieldsel_1_imm};  // Bit_Extender bit_extender_3
  ALUCtrl aluctrl_1 (.funct(fieldsel_1_funct), .ALUop(aluctrl_1_aluop[3:0]), .ALUfn(mainctrl_1_alufn));
  Shifter #(.width(32)) shifter_1 (.in(bit_extender_3_out), .\dist (5'b00010), .out(shifter_1_out));
  BitSelector #(.width(32), .group(4)) bitselector_1 (
    .in(subtractor_1_out), .out(fieldsel_1_instr_ind[31:28]), .sel(3'b111));
  Multiplexer #(.width(32), .enable("false")) multiplexer_5 (
    .in0(bit_extender_2_out), .in1(bit_extender_3_out), .out(multiplexer_5_out), .sel(mainctrl_1_extsign));
  Adder #(.width(32)) adder_3 (.a(D_pc4_q), .b(shifter_1_out), .out(adder_3_out));  // open: cin, cout
  Multiplexer #(.width(32), .enable("false")) multiplexer_6 (
    .in0(adder_2_out), .in1(adder_3_out), .out(multiplexer_6_out), .sel(comparator_1_eq));
  // Probe on grf_1_rdat1
  GRF grf_1 (
    .radd1(fieldsel_1_rs), .radd2(fieldsel_1_rt), .wadd(RegAddr), .wdat(RegData), .CLK(clock_1_out),
    .RST(Reset), .GRFwen(RegWrite), .rdat1(grf_1_rdat1), .rdat2(grf_1_rdat2));
  // Probe on grf_1_rdat2
  // Probe on multiplexer_5_out
  Multiplexer #(.select(2), .width(5), .enable("false")) multiplexer_7 (
    .in0(fieldsel_1_rt), .in1(fieldsel_1_rd), .in2({5{1'b1}}), .out(multiplexer_7_out),
    .sel(mainctrl_1_grfwen[4:3]));  // open: in3
  Multiplexer #(.select(2), .width(32), .enable("false")) multiplexer_8 (
    .in0(grf_1_rdat1), .in1(M_addr_q), .in2(M_pc8_q), .in3(E_pc8_q), .out(multiplexer_8_out),
    .sel(dfwctrl_1_fw1));
  // Probe on multiplexer_8_out
  Multiplexer #(.select(2), .width(32), .enable("false")) multiplexer_9 (
    .in0(grf_1_rdat2), .in1(M_addr_q), .in2(M_pc8_q), .in3(E_pc8_q), .out(multiplexer_9_out),
    .sel(dfwctrl_1_fw2));
  // Probe on multiplexer_9_out
  DFWCtrl dfwctrl_1 (
    .Drreg1(fieldsel_1_rs), .Drreg2(fieldsel_1_rt), .Mwreg(M_wreg_q), .Mtnew(M_tnew_q),
    .MGRFwen(M_WCtrl_q[0]), .fw1(dfwctrl_1_fw1), .fw2(dfwctrl_1_fw2), .MGRFwdst(M_WCtrl_q_2),
    .Ewreg(E_wreg_q), .Etnew(E_tnew_q), .EGRFwen(E_WCtrl_q[0]), .EGRFwdst(E_WCtrl_q_2));
  Comparator #(.width(32)) comparator_1 (
    .a(multiplexer_8_out), .b(multiplexer_9_out), .eq(comparator_1_eq));  // open: gt, lt
  Register #(.width(32)) E_pc8 (.D(adder_2_out), .Q(E_pc8_q), .clk(clock_1_out), .clr(Reset));  // open: en
  Register #(.width(32)) E_npc (.D(D_npc_q), .Q(E_npc_q), .clk(clock_1_out), .clr(Reset));  // open: en
  Register #(.width(5)) E_shamt (.D(fieldsel_1_shamt), .Q(E_shamt_q), .clk(clock_1_out), .clr(Reset));  // open: en
  Register #(.width(32)) E_rd1 (.D(multiplexer_8_out), .Q(E_rd1_q), .clk(clock_1_out), .clr(Reset));  // open: en
  Register #(.width(32)) E_rd2 (.D(multiplexer_9_out), .Q(E_rd2_q), .clk(clock_1_out), .clr(Reset));  // open: en
  Register #(.width(32)) E_imm (.D(multiplexer_5_out), .Q(E_imm_q), .clk(clock_1_out), .clr(Reset));  // open: en
  Register #(.width(6)) E_ECtrl (.D(aluctrl_1_aluop), .Q(E_ECtrl_q), .clk(clock_1_out), .clr(Reset));  // open: en
  Register #(.width(5)) E_WCtrl (
    .D(mainctrl_1_grfwen), .Q({E_WCtrl_q_2, E_WCtrl_q}), .clk(clock_1_out), .clr(Reset));  // open: en
  Register #(.width(2)) E_MCtrl (.D(mainctrl_1_dmwrstate), .Q(E_MCtrl_q), .clk(clock_1_out), .clr(Reset));  // open: en
  Register #(.width(5)) E_wreg (.D(multiplexer_7_out), .Q(E_wreg_q), .clk(clock_1_out), .clr(Reset));  // open: en
  Register #(.width(5)) E_rreg1 (.D(fieldsel_1_rs), .Q(E_rreg1_q), .clk(clock_1_out), .clr(Reset));  // open: en
  Register #(.width(5)) E_rreg2 (.D(fieldsel_1_rt), .Q(E_rreg2_q), .clk(clock_1_out), .clr(Reset));  // open: en
  Register #(.width(2)) E_tnew (.D(mainctrl_1_tninit), .Q(E_tnew_q), .clk(clock_1_out), .clr(Reset));  // open: en
  // Probe on E_npc_q
  Multiplexer #(.select(3), .width(32), .enable("false")) multiplexer_10 (
    .in0(E_rd2_q), .in1(RegData), .in2(M_addr_q), .in4(E_rd2_q), .in5(W_pc8_q), .in6(M_pc8_q),
    .out(multiplexer_10_out), .sel(efwctrl_1_fw2));  // open: in3, in7
  Multiplexer #(.width(5), .enable("false")) multiplexer_11 (
    .in0(E_shamt_q), .in1(5'b10000), .out(multiplexer_11_out), .sel(E_ECtrl_q[4]));
  // Probe on multiplexer_11_out
  // Probe on multiplexer_12_out
  Multiplexer #(.select(3), .width(32), .enable("false")) multiplexer_12 (
    .in0(E_rd1_q), .in1(RegData), .in2(M_addr_q), .in4(E_rd1_q), .in5(W_pc8_q), .in6(M_pc8_q),
    .out(multiplexer_12_out), .sel(efwctrl_1_fw1));  // open: in3, in7
  Multiplexer #(.width(32), .enable("false")) multiplexer_13 (
    .in0(multiplexer_10_out), .in1(E_imm_q), .out(multiplexer_13_out), .sel(E_ECtrl_q[5]));
  EFWCtrl efwctrl_1 (
    .Mwreg(M_wreg_q), .Wwreg(RegAddr), .Mtnew(M_tnew_q), .Wtnew(W_tnew_q), .MGRFwen(M_WCtrl_q[0]),
    .WGRFwen(RegWrite), .fw1(efwctrl_1_fw1), .fw2(efwctrl_1_fw2), .Erreg1(E_rreg1_q), .Erreg2(E_rreg2_q),
    .MGRFwdst(M_WCtrl_q_2), .WGRFwdst(W_WCtrl_q[4:3]));
  MUDV mudv_1 (
    .mdop(undriven_3), .clk(clock_1_out), .opa(multiplexer_12_out), .opb(multiplexer_13_out),
    .busy(mudv_1_busy), .lo(mudv_1_lo), .hi(mudv_1_hi), .write_en(undriven), .start(undriven_2));
  // Probe on multiplexer_13_out
  ALU alu_1 (
    .op1(multiplexer_12_out), .op2(multiplexer_13_out), .res(alu_1_res), .ALUop(E_ECtrl_q[3:0]),
    .shamt(multiplexer_11_out));
  Comparator #(.width(2)) comparator_2 (.a(E_tnew_q), .b(2'b00), .eq(comparator_2_eq));  // open: gt, lt
  Subtractor #(.width(2)) subtractor_2 (.a(E_tnew_q), .b(2'b01), .out(subtractor_2_out));  // open: bin, bout
  Multiplexer #(.select(2), .width(32), .enable("false")) multiplexer_14 (
    .in0(alu_1_res), .in1(mudv_1_lo), .in2(mudv_1_hi), .out(multiplexer_14_out), .sel(undriven_4));  // open: in3
  Multiplexer #(.width(2), .enable("false")) multiplexer_15 (
    .in0(subtractor_2_out), .in1(E_tnew_q), .out(multiplexer_15_out), .sel(comparator_2_eq));
  Register #(.width(32)) M_pc8 (.D(E_pc8_q), .Q(M_pc8_q), .clk(clock_1_out), .clr(Reset));  // open: en
  // Probe on npc
  Register #(.width(32)) M_npc (.D(E_npc_q), .Q(npc), .clk(clock_1_out), .clr(Reset));  // open: en
  Register #(.width(32)) M_addr (.D(multiplexer_14_out), .Q(M_addr_q), .clk(clock_1_out), .clr(Reset));  // open: en
  Register #(.width(32)) M_DMwdat (.D(multiplexer_10_out), .Q(M_DMwdat_q), .clk(clock_1_out), .clr(Reset));  // open: en
  Register #(.width(5)) M_WCtrl (
    .D({E_WCtrl_q_2, E_WCtrl_q}), .Q({M_WCtrl_q_2, M_WCtrl_q}), .clk(clock_1_out), .clr(Reset));  // open: en
  Register #(.width(2)) M_MCtrl (.D(E_MCtrl_q), .Q(M_MCtrl_q), .clk(clock_1_out), .clr(Reset));  // open: en
  Register #(.width(5)) M_wreg (.D(E_wreg_q), .Q(M_wreg_q), .clk(clock_1_out), .clr(Reset));  // open: en
  Register #(.width(5)) M_rreg2 (.D(E_rreg2_q), .Q(M_rreg2_q), .clk(clock_1_out), .clr(Reset));  // open: en
  Register #(.width(2)) M_tnew (.D(multiplexer_15_out), .Q(M_tnew_q), .clk(clock_1_out), .clr(Reset));  // open: en
  Multiplexer #(.width(32), .enable("false")) multiplexer_16 (
    .in0(M_DMwdat_q), .in1(RegData), .out(multiplexer_16_out), .sel(sfwctrl_1_fw2));
  // Probe on M_addr_q
  // Probe on multiplexer_16_out
  SFWCtrl sfwctrl_1 (.Mrreg2(M_rreg2_q), .Wwreg(RegAddr), .Wtnew(W_tnew_q), .WGRFwen(RegWrite), .fw2(sfwctrl_1_fw2));
  DataMem datamem_1 (
    .addr(M_addr_q), .wdat(multiplexer_16_out), .rdat(datamem_1_rdat), .CLK(clock_1_out),
    .DMwrite(M_MCtrl_q[1]), .RST(Reset), .DMread(M_MCtrl_q[0]));
  // Probe on datamem_1_rdat
  Comparator #(.width(2)) comparator_3 (.a(M_tnew_q), .b(2'b00), .eq(comparator_3_eq));  // open: gt, lt
  Subtractor #(.width(2)) subtractor_3 (.a(M_tnew_q), .b(2'b01), .out(subtractor_3_out));  // open: bin, bout
  Multiplexer #(.width(2), .enable("false")) multiplexer_17 (
    .in0(subtractor_3_out), .in1(M_tnew_q), .out(multiplexer_17_out), .sel(comparator_3_eq));
  Register #(.width(32)) W_pc8 (.D(M_pc8_q), .Q(W_pc8_q), .clk(clock_1_out), .clr(Reset));  // open: en
  Register #(.width(32)) W_npc (.D(npc), .clk(clock_1_out), .clr(Reset));  // open: en, Q
  Register #(.width(32)) W_alures (.D(M_addr_q), .Q(MemAddr), .clk(clock_1_out), .clr(Reset));  // open: en
  Register #(.width(32)) W_dmrdat (.D(datamem_1_rdat), .Q(W_dmrdat_q), .clk(clock_1_out), .clr(Reset));  // open: en
  Register #(.width(5)) W_WCtrl (
    .D({M_WCtrl_q_2, M_WCtrl_q}), .Q({W_WCtrl_q, RegWrite}), .clk(clock_1_out), .clr(Reset));  // open: en
  Register #(.width(32)) W_DMwdat (.D(multiplexer_16_out), .Q(MemData), .clk(clock_1_out), .clr(Reset));  // open: en
  Register #(.width(2)) W_MCtrl (
    .D(M_MCtrl_q), .Q({MemWrite, W_MCtrl_q[0]}), .clk(clock_1_out), .clr(Reset));  // open: en
  Register #(.width(5)) W_wreg (.D(M_wreg_q), .Q(RegAddr), .clk(clock_1_out), .clr(Reset));  // open: en
  Register #(.width(2)) W_tnew (.D(multiplexer_17_out), .Q(W_tnew_q), .clk(clock_1_out), .clr(Reset));  // open: en
  // Probe on RegAddr
  Multiplexer #(.select(2), .width(32), .enable("false")) multiplexer_18 (
    .in0(MemAddr), .in1(W_dmrdat_q), .in2(W_pc8_q), .out(RegData), .sel(W_WCtrl_q[2:1]));  // open: in3
  // Probe on RegData

  // Other names for the same wires on the sheet: pc[31:0] = out_5

  // Notes on the sheet:
  //   TestBench
  //   pc+4
  //   GRFwen
  //   GRFwdst
  //   GRFwdatsrc
  //   ALUshsrc
  //   ALUien
  //   EXTsign
  //   PCsrc
  //   DMstate
  //   TNinit
  //   jump to reg
  //   jump jadd
  //   pc+4+offset
  //   Epc8
  //   Mpc8
  //   Mres
  //   Wpc8
  //   Wdat
endmodule

module PC (
  input  [31:0] npc,
  input  RST,
  input  pcen,
  input  CLK,
  output [31:0] pc
);

  wire [31:0] multiplexer_1_out, register_1_q, subtractor_1_out;

  // Probe on npc
  Subtractor #(.width(32)) subtractor_1 (.a(npc), .b(32'h3000), .out(subtractor_1_out));  // open: bin, bout
  Multiplexer #(.width(32), .enable("false")) multiplexer_1 (
    .in0(subtractor_1_out), .in1({32{1'b0}}), .out(multiplexer_1_out), .sel(RST));
  Register #(.width(32)) register_1 (.D(multiplexer_1_out), .en(pcen), .Q(register_1_q), .clk(CLK));  // open: clr
  // Probe on pc
  Adder #(.width(32)) adder_1 (.a(register_1_q), .b(32'h3000), .out(pc));  // open: cin, cout
endmodule

module InstrMem (
  input  [31:0] pc,
  output [31:0] instr
);

  wire [11:0] bitselector_1_out;
  wire [31:0] shifter_1_out, subtractor_1_out;

  // Probe on subtractor_1_out
  Subtractor #(.width(32)) subtractor_1 (.a(pc), .b(32'h3000), .out(subtractor_1_out));  // open: bin, bout
  Shifter #(.width(32), .shift("lr")) shifter_1 (.in(subtractor_1_out), .\dist (5'b00010), .out(shifter_1_out));
  BitSelector #(.width(32), .group(12)) bitselector_1 (.in(shifter_1_out), .out(bitselector_1_out), .sel(2'b00));
  ROM #(.addrWidth(12), .dataWidth(32)) rom_1 (.addr(bitselector_1_out), .data(instr));  // open: sel
  // Probe on instr

  // Notes on the sheet:
  //   contents of rom_1 (hex, n*v repeats v):
  //   341f3010 3e00008 0 34011145 34014511
endmodule

module FieldSel (
  input  [31:0] instr,
  output [4:0] shamt,
  output [4:0] rs,
  output [4:0] rt,
  output [4:0] rd,
  output [15:0] imm,
  output [25:0] instr_ind,
  output [5:0] opcode,
  output [5:0] funct
);


  assign funct = instr[5:0];
  assign imm = instr[15:0];
  assign instr_ind = instr[25:0];
  assign opcode = instr[31:26];
  assign rd = instr[15:11];
  assign rs = instr[25:21];
  assign rt = instr[20:16];
  assign shamt = instr[10:6];
endmodule

module GRF (
  input  [4:0] radd1,
  input  [4:0] radd2,
  input  [4:0] wadd,
  input  [31:0] wdat,
  input  GRFwen,
  input  CLK,
  input  RST,
  output [31:0] rdat1,
  output [31:0] rdat2
);

  wire and_1_out, and_2_out, comparator_1_eq, comparator_2_eq, comparator_3_eq, comparator_4_eq, RST_t;
  wire [31:0] multiplexer_3_out, multiplexer_4_out, r0, r0o, r1, r1o, r2, r2o, r3, r3o, r4, r4o, r5, r5o, r6,
       r6o, r7, r7o, r8, r8o, r9, r9o, r10, r10o, r11, r11o, r12, r12o, r13, r13o, r14, r14o, r15, r15o, r16,
       r16o, r17, r17o, r18, r18o, r19, r19o, r20, r20o, r21, r21o, r22, r22o, r23, r23o, r24, r24o, r25,
       r25o, r26, r26o, r27, r27o, r28, r28o, r29, r29o, r30, r30o, r31, r31o, read_data1, read_data2;

  Multiplexer #(.select(5), .width(32), .enable("false")) multiplexer_1 (
    .in0(r0o), .in1(r1o), .in2(r2o), .in3(r3o), .in4(r4o), .in5(r5o), .in6(r6o), .in7(r7o), .in8(r8o),
    .in9(r9o), .in10(r10o), .in11(r11o), .in12(r12o), .in13(r13o), .in14(r14o), .in15(r15o), .in16(r16o),
    .in17(r17o), .in18(r18o), .in19(r19o), .in20(r20o), .in21(r21o), .in22(r22o), .in23(r23o), .in24(r24o),
    .in25(r25o), .in26(r26o), .in27(r27o), .in28(r28o), .in29(r29o), .in30(r30o), .in31(r31o),
    .out(read_data1), .sel(radd1));
  D_Flip_Flop d_ff_1 (.clk(CLK), .D(RST), .Q(RST_t));  // open: Qn, preset, en, reset
  Multiplexer #(.select(5), .width(32), .enable("false")) multiplexer_2 (
    .in0(r0o), .in1(r1o), .in2(r2o), .in3(r3o), .in4(r4o), .in5(r5o), .in6(r6o), .in7(r7o), .in8(r8o),
    .in9(r9o), .in10(r10o), .in11(r11o), .in12(r12o), .in13(r13o), .in14(r14o), .in15(r15o), .in16(r16o),
    .in17(r17o), .in18(r18o), .in19(r19o), .in20(r20o), .in21(r21o), .in22(r22o), .in23(r23o), .in24(r24o),
    .in25(r25o), .in26(r26o), .in27(r27o), .in28(r28o), .in29(r29o), .in30(r30o), .in31(r31o),
    .out(read_data2), .sel(radd2));
  Register #(.width(32)) register_1 (.D({32{1'b0}}), .en(1'b1), .Q(r0o), .clk(CLK), .clr(RST_t));
  Register #(.width(32)) register_2 (.D(r8), .en(1'b1), .Q(r8o), .clk(CLK), .clr(RST_t));
  Register #(.width(32)) register_3 (.D(r16), .en(1'b1), .Q(r16o), .clk(CLK), .clr(RST_t));
  Register #(.width(32)) register_4 (.D(r24), .en(1'b1), .Q(r24o), .clk(CLK), .clr(RST_t));
  Register #(.width(32)) register_5 (.D(r1), .en(1'b1), .Q(r1o), .clk(CLK), .clr(RST_t));
  Register #(.width(32)) register_6 (.D(r9), .en(1'b1), .Q(r9o), .clk(CLK), .clr(RST_t));
  Register #(.width(32)) register_7 (.D(r17), .en(1'b1), .Q(r17o), .clk(CLK), .clr(RST_t));
  Register #(.width(32)) register_8 (.D(r25), .en(1'b1), .Q(r25o), .clk(CLK), .clr(RST_t));
  Multiplexer #(.select(5), .width(32), .enable("false")) multiplexer_3 (
    .in0(r0o), .in1(r1o), .in2(r2o), .in3(r3o), .in4(r4o), .in5(r5o), .in6(r6o), .in7(r7o), .in8(r8o),
    .in9(r9o), .in10(r10o), .in11(r11o), .in12(r12o), .in13(r13o), .in14(r14o), .in15(r15o), .in16(r16o),
    .in17(r17o), .in18(r18o), .in19(r19o), .in20(r20o), .in21(r21o), .in22(r22o), .in23(r23o), .in24(r24o),
    .in25(r25o), .in26(r26o), .in27(r27o), .in28(r28o), .in29(r29o), .in30(r30o), .in31(r31o),
    .out(multiplexer_3_out), .sel(wadd));
  Register #(.width(32)) register_9 (.D(r2), .en(1'b1), .Q(r2o), .clk(CLK), .clr(RST_t));
  Register #(.width(32)) register_10 (.D(r10), .en(1'b1), .Q(r10o), .clk(CLK), .clr(RST_t));
  Register #(.width(32)) register_11 (.D(r18), .en(1'b1), .Q(r18o), .clk(CLK), .clr(RST_t));
  Register #(.width(32)) register_12 (.D(r26), .en(1'b1), .Q(r26o), .clk(CLK), .clr(RST_t));
  Multiplexer #(.width(32), .enable("false")) multiplexer_4 (
    .in0(multiplexer_3_out), .in1(wdat), .out(multiplexer_4_out), .sel(GRFwen));
  Demultiplexer #(.select(5), .width(32), .tristate("true"), .enable("false")) demultiplexer_1 (
    .out0(r0), .out1(r1), .out2(r2), .out3(r3), .out4(r4), .out5(r5), .out6(r6), .out7(r7), .out8(r8),
    .out9(r9), .out10(r10), .out11(r11), .out12(r12), .out13(r13), .out14(r14), .out15(r15), .out16(r16),
    .out17(r17), .out18(r18), .out19(r19), .out20(r20), .out21(r21), .out22(r22), .out23(r23), .out24(r24),
    .out25(r25), .out26(r26), .out27(r27), .out28(r28), .out29(r29), .out30(r30), .out31(r31),
    .in(multiplexer_4_out), .sel(wadd));
  Register #(.width(32)) register_13 (.D(r3), .en(1'b1), .Q(r3o), .clk(CLK), .clr(RST_t));
  Register #(.width(32)) register_14 (.D(r11), .en(1'b1), .Q(r11o), .clk(CLK), .clr(RST_t));
  Register #(.width(32)) register_15 (.D(r19), .en(1'b1), .Q(r19o), .clk(CLK), .clr(RST_t));
  Register #(.width(32)) register_16 (.D(r27), .en(1'b1), .Q(r27o), .clk(CLK), .clr(RST_t));
  Register #(.width(32)) register_17 (.D(r4), .en(1'b1), .Q(r4o), .clk(CLK), .clr(RST_t));
  Register #(.width(32)) register_18 (.D(r12), .en(1'b1), .Q(r12o), .clk(CLK), .clr(RST_t));
  Register #(.width(32)) register_19 (.D(r20), .en(1'b1), .Q(r20o), .clk(CLK), .clr(RST_t));
  Register #(.width(32)) register_20 (.D(r28), .en(1'b1), .Q(r28o), .clk(CLK), .clr(RST_t));
  Register #(.width(32)) register_21 (.D(r5), .en(1'b1), .Q(r5o), .clk(CLK), .clr(RST_t));
  Register #(.width(32)) register_22 (.D(r13), .en(1'b1), .Q(r13o), .clk(CLK), .clr(RST_t));
  Register #(.width(32)) register_23 (.D(r21), .en(1'b1), .Q(r21o), .clk(CLK), .clr(RST_t));
  Register #(.width(32)) register_24 (.D(r29), .en(1'b1), .Q(r29o), .clk(CLK), .clr(RST_t));
  Register #(.width(32)) register_25 (.D(r6), .en(1'b1), .Q(r6o), .clk(CLK), .clr(RST_t));
  Register #(.width(32)) register_26 (.D(r14), .en(1'b1), .Q(r14o), .clk(CLK), .clr(RST_t));
  Register #(.width(32)) register_27 (.D(r22), .en(1'b1), .Q(r22o), .clk(CLK), .clr(RST_t));
  Register #(.width(32)) register_28 (.D(r30), .en(1'b1), .Q(r30o), .clk(CLK), .clr(RST_t));
  and and_1 (and_1_out, comparator_1_eq, ~comparator_2_eq, GRFwen);  // AND_Gate
  Comparator #(.width(5)) comparator_1 (.a(wadd), .b(radd1), .eq(comparator_1_eq));  // open: gt, lt
  Comparator #(.width(5)) comparator_2 (.a(radd1), .b({5{1'b0}}), .eq(comparator_2_eq));  // open: gt, lt
  and and_2 (and_2_out, comparator_3_eq, ~comparator_4_eq, GRFwen);  // AND_Gate
  Comparator #(.width(5)) comparator_3 (.a(wadd), .b(radd2), .eq(comparator_3_eq));  // open: gt, lt
  Comparator #(.width(5)) comparator_4 (.a(radd2), .b({5{1'b0}}), .eq(comparator_4_eq));  // open: gt, lt
  Register #(.width(32)) register_29 (.D(r7), .en(1'b1), .Q(r7o), .clk(CLK), .clr(RST_t));
  Register #(.width(32)) register_30 (.D(r15), .en(1'b1), .Q(r15o), .clk(CLK), .clr(RST_t));
  Register #(.width(32)) register_31 (.D(r23), .en(1'b1), .Q(r23o), .clk(CLK), .clr(RST_t));
  Register #(.width(32)) register_32 (.D(r31), .en(1'b1), .Q(r31o), .clk(CLK), .clr(RST_t));
  Multiplexer #(.width(32), .enable("false")) multiplexer_5 (
    .in0(read_data1), .in1(wdat), .out(rdat1), .sel(and_1_out));
  Multiplexer #(.width(32), .enable("false")) multiplexer_6 (
    .in0(read_data2), .in1(wdat), .out(rdat2), .sel(and_2_out));

  // Other names for the same wires on the sheet: IN[31:0] = wdat; read1[4:0] = radd1; read2[4:0] = radd2;
  //   WEN = GRFwen; write[4:0] = wadd

  // Notes on the sheet:
  //   interfaces
  //   output
  //   registers
  //   input
endmodule

module ALU (
  input  [3:0] ALUop,
  input  [31:0] op1,
  input  [31:0] op2,
  input  [4:0] shamt,
  output [31:0] res
);

  wire [31:0] adder_1_out, and_1_out, or_1_out, shifter_1_out, shifter_2_out, shifter_3_out, subtractor_1_out;

  Shifter #(.width(32)) shifter_1 (.in(op2), .\dist (shamt), .out(shifter_1_out));
  Shifter #(.width(32), .shift("lr")) shifter_2 (.in(op2), .\dist (shamt), .out(shifter_2_out));
  Shifter #(.width(32), .shift("ar")) shifter_3 (.in(op2), .\dist (shamt), .out(shifter_3_out));
  Adder #(.width(32)) adder_1 (.a(op1), .b(op2), .out(adder_1_out));  // open: cin, cout
  Subtractor #(.width(32)) subtractor_1 (.a(op1), .b(op2), .out(subtractor_1_out));  // open: bin, bout
  assign and_1_out = op1 & op2;  // AND_Gate and_1, 32 bits wide
  assign or_1_out = op1 | op2;  // OR_Gate or_1, 32 bits wide
  Multiplexer #(.select(4), .width(32), .enable("false")) multiplexer_1 (
    .in0(shifter_1_out), .in1(shifter_2_out), .in2(shifter_3_out), .in3(adder_1_out), .in4(subtractor_1_out),
    .in5(and_1_out), .in6(or_1_out), .out(res), .sel(ALUop));  // open: in7, in8, in9, in10, in11, in12, in13, in14, in15
endmodule

module DataMem (
  input  [31:0] addr,
  input  DMwrite,
  input  DMread,
  input  [31:0] wdat,
  input  CLK,
  input  RST,
  output [31:0] rdat
);

  wire d_ff_1_q;
  wire [11:0] bitselector_1_out;
  wire [31:0] shifter_1_out;

  Shifter #(.width(32), .shift("lr")) shifter_1 (.in(addr), .\dist (5'b00010), .out(shifter_1_out));
  BitSelector #(.width(32), .group(12)) bitselector_1 (.in(shifter_1_out), .out(bitselector_1_out), .sel(2'b00));
  RAM #(.addrWidth(12), .dataWidth(32), .bus("separate")) ram_1 (
    .addr(bitselector_1_out), .din(wdat), .data(rdat), .str(DMwrite), .clk(CLK), .ld(DMread), .clr(d_ff_1_q));  // open: sel
  D_Flip_Flop d_ff_1 (.clk(CLK), .D(RST), .Q(d_ff_1_q));  // open: Qn, preset, en, reset
endmodule

module ALUCtrl (
  input  [5:0] funct,
  input  [3:0] ALUfn,
  output [3:0] ALUop
);

  wire comparator_1_eq, comparator_2_eq, not_1_out;
  wire [1:0] bitselector_3_out;
  wire [2:0] bitselector_1_out, bitselector_2_out;
  wire [3:0] multiplexer_1_out, multiplexer_2_out, multiplexer_3_out, multiplexer_4_out;

  BitSelector #(.width(6), .group(3)) bitselector_1 (.in(funct), .out(bitselector_1_out), .sel(1'b1));
  BitSelector #(.width(6), .group(3)) bitselector_2 (.in(funct), .out(bitselector_2_out), .sel(1'b0));
  BitSelector #(.width(3), .group(2)) bitselector_3 (.in(bitselector_2_out), .out(bitselector_3_out), .sel(1'b0));
  Multiplexer #(.select(2), .width(4), .enable("false")) multiplexer_1 (
    .in0(4'b0000), .in2(4'b0001), .in3(4'b0010), .out(multiplexer_1_out), .sel(bitselector_3_out));  // open: in1
  Multiplexer #(.select(3), .width(4), .enable("false")) multiplexer_2 (
    .in0(4'b0011), .in2(4'b0100), .in4(4'b0101), .in5(4'b0110), .in6(4'b0111), .in7(4'b1000),
    .out(multiplexer_2_out), .sel(bitselector_2_out));  // open: in1, in3
  Multiplexer #(.select(3), .width(4), .enable("false")) multiplexer_3 (
    .in0(multiplexer_1_out), .in4(multiplexer_2_out), .in5(4'b1001), .out(multiplexer_3_out),
    .sel(bitselector_1_out));  // open: in1, in2, in3, in6, in7
  Pull_Resistor pull_resistor_1 (.node(ALUfn));
  Multiplexer #(.width(4), .enable("false")) multiplexer_4 (
    .in0(multiplexer_3_out), .in1(ALUfn), .out(multiplexer_4_out), .sel(not_1_out));
  not not_1 (not_1_out, comparator_1_eq);
  Comparator #(.width(4), .mode("unsigned")) comparator_1 (
    .a(ALUfn), .b(4'b0000), .eq(comparator_1_eq));  // open: gt, lt
  Comparator #(.width(4), .mode("unsigned")) comparator_2 (
    .a(ALUfn), .b(4'b1111), .eq(comparator_2_eq));  // open: gt, lt
  Multiplexer #(.width(4), .enable("false")) multiplexer_5 (
    .in0(multiplexer_4_out), .in1(4'b0000), .out(ALUop), .sel(comparator_2_eq));
endmodule

module MainCtrl (
  input  [5:0] funct,
  input  [5:0] opcode,
  output GRFwen,
  output [1:0] GRFwdst,
  output [1:0] GRFwdatsrc,
  output [3:0] ALUfn,
  output ALUshsrc,
  output ALUien,
  output EXTsign,
  output [1:0] PCsrc,
  output [1:0] DMwrstate,
  output [1:0] TNinit
);

  wire and_1_out, and_2_out, and_3_out, and_4_out, and_5_out, bitselector_3_out, comparator_1_eq,
       decoder_1_out0, decoder_1_out1, decoder_1_out4, decoder_1_out5, decoder_2_out0, decoder_2_out1,
       decoder_2_out3, decoder_3_out4, decoder_3_out5, decoder_3_out6, not_2_out, or_1_out, or_2_out,
       or_3_out, or_5_out, or_6_out;
  wire [1:0] priority_encoder_4_out;
  wire [2:0] bitselector_1_out, bitselector_2_out;

  BitSelector #(.width(6), .group(3)) bitselector_1 (.in(opcode), .out(bitselector_1_out), .sel(1'b1));
  BitSelector #(.width(6), .group(3)) bitselector_2 (.in(opcode), .out(bitselector_2_out), .sel(1'b0));
  Decoder #(.select(3), .disabled(0), .enable("false")) decoder_1 (
    .out0(decoder_1_out0), .out1(decoder_1_out1), .out4(decoder_1_out4), .out5(decoder_1_out5),
    .sel(bitselector_1_out));  // open: out2, out3, out6, out7
  and and_1 (and_1_out, decoder_1_out0, ~or_1_out);  // AND_Gate
  BitSelector #(.width(3)) bitselector_3 (.in(bitselector_2_out), .out(bitselector_3_out), .sel(2'b10));
  or or_1 (or_1_out, decoder_2_out0, decoder_2_out1);
  and and_2 (and_2_out, and_1_out, bitselector_3_out);
  and and_3 (and_3_out, and_1_out, ~bitselector_3_out);  // AND_Gate
  Decoder #(.select(3), .disabled(0)) decoder_2 (
    .out0(decoder_2_out0), .out1(decoder_2_out1), .out3(decoder_2_out3), .sel(bitselector_2_out),
    .en(decoder_1_out0));  // open: out2, out4, out5, out6, out7
  Comparator #(.width(6)) comparator_1 (.a(funct), .b(6'b001000), .eq(comparator_1_eq));  // open: gt, lt
  Decoder #(.select(3), .disabled(0)) decoder_3 (
    .out4(decoder_3_out4), .out5(decoder_3_out5), .out6(decoder_3_out6), .out7(ALUshsrc),
    .sel(bitselector_2_out), .en(decoder_1_out1));  // open: out0, out1, out2, out3
  and and_4 (and_4_out, comparator_1_eq, decoder_2_out0);
  Decoder #(.select(3), .disabled(0)) decoder_4 (
    .sel(bitselector_2_out), .en(decoder_1_out4));  // open: out0, out1, out2, out3, out4, out5, out6, out7
  or or_2 (or_2_out, and_4_out, decoder_2_out3);
  Decoder #(.select(3), .disabled(0)) decoder_5 (
    .sel(bitselector_2_out), .en(decoder_1_out5));  // open: out0, out1, out2, out3, out4, out5, out6, out7
  or or_3 (or_3_out, decoder_1_out4, decoder_1_out5);
  or or_4 (ALUien, decoder_1_out5, decoder_1_out4, decoder_1_out1);
  or or_5 (or_5_out, decoder_3_out4, decoder_3_out5, decoder_3_out6);
  or or_6 (or_6_out, decoder_1_out1, decoder_2_out0);
  and and_5 (and_5_out, ~decoder_1_out5, ~and_1_out);  // AND_Gate
  Priority_Encoder #(.select(2)) priority_encoder_1 (
    .in0(1'b1), .in1(decoder_2_out0), .in2(decoder_2_out3), .out(GRFwdst));  // open: in3, gs, en_out, en_in
  Priority_Encoder #(.select(2)) priority_encoder_2 (
    .in0(1'b1), .in1(decoder_1_out4), .in2(decoder_2_out3), .out(GRFwdatsrc));  // open: in3, gs, en_out, en_in
  Priority_Encoder #(.select(4)) priority_encoder_3 (
    .in0(1'b1), .in3(or_3_out), .in4(and_1_out), .in6(decoder_3_out5), .in15(ALUshsrc), .out(ALUfn));  // open: in1, in2, in5, in7, in8, in9, in10, in11, in12, in13, in14, gs, en_out, en_in
  not not_1 (EXTsign, or_5_out);
  Priority_Encoder #(.select(2)) priority_encoder_4 (
    .in0(1'b1), .in1(and_2_out), .in2(and_3_out), .out(priority_encoder_4_out));  // open: in3, gs, en_out, en_in
  Priority_Encoder #(.select(2)) priority_encoder_5 (
    .in0(1'b1), .in1(decoder_1_out4), .in2(decoder_1_out5), .out(DMwrstate));  // open: in3, gs, en_out, en_in
  Priority_Encoder #(.select(2)) priority_encoder_6 (
    .in0(1'b1), .in1(or_6_out), .in2(decoder_1_out4), .out(TNinit));  // open: in3, gs, en_out, en_in
  Multiplexer #(.enable("false")) multiplexer_1 (.in0(and_5_out), .in1(not_2_out), .out(GRFwen), .sel(or_2_out));
  not not_2 (not_2_out, and_5_out);
  Multiplexer #(.width(2), .enable("false")) multiplexer_2 (
    .in0(priority_encoder_4_out), .in1(2'b11), .out(PCsrc), .sel(and_4_out));

  // Notes on the sheet:
  //   Store
  //   Load
  //   Imm
  //   J&B
  //   R-type+?
  //   R-type
  //   Bran
  //   Jmp
  //   R,J,B
  //   Imm
  //   special for JR & JAL
  //   JR
  //   Load
  //   Store
endmodule

module DFWCtrl (
  input  [4:0] Drreg1,
  input  [4:0] Drreg2,
  input  [4:0] Mwreg,
  input  [4:0] Ewreg,
  input  [1:0] Mtnew,
  input  [1:0] Etnew,
  input  MGRFwen,
  input  [1:0] MGRFwdst,
  input  EGRFwen,
  input  [1:0] EGRFwdst,
  output [1:0] fw1,
  output [1:0] fw2
);

  wire and_1_out, and_2_out, and_3_out, and_4_out, comparator_1_eq, comparator_2_eq, comparator_3_eq,
       comparator_4_eq, comparator_5_eq, comparator_6_eq, comparator_7_eq, comparator_8_eq, comparator_9_eq,
       comparator_10_eq, controlled_buffer_1_out, controlled_buffer_3_out, controlled_buffer_4_out,
       controlled_buffer_5_out, controlled_buffer_6_out, pull_resistor_2_node;

  assign controlled_buffer_1_out = and_1_out ? comparator_1_eq : 1'bz;  // Controlled_Buffer controlled_buffer_1
  Pull_Resistor pull_resistor_1 (.node(controlled_buffer_1_out));
  Comparator #(.width(5)) comparator_1 (.a(Drreg1), .b(Mwreg), .eq(comparator_1_eq));  // open: gt, lt
  Comparator #(.width(5)) comparator_2 (.a(Drreg2), .b(Mwreg), .eq(comparator_2_eq));  // open: gt, lt
  Pull_Resistor pull_resistor_2 (.node(pull_resistor_2_node));
  assign pull_resistor_2_node = and_1_out ? comparator_2_eq : 1'bz;  // Controlled_Buffer controlled_buffer_2
  Comparator #(.width(5)) comparator_3 (.a(Mwreg), .b({5{1'b0}}), .eq(comparator_3_eq));  // open: gt, lt
  and and_1 (and_1_out, comparator_4_eq, ~comparator_3_eq, MGRFwen);  // AND_Gate
  Comparator #(.width(2)) comparator_4 (.a(2'b00), .b(Mtnew), .eq(comparator_4_eq));  // open: gt, lt
  assign controlled_buffer_3_out = and_2_out ? comparator_1_eq : 1'bz;  // Controlled_Buffer controlled_buffer_3
  Pull_Resistor pull_resistor_3 (.node(controlled_buffer_3_out));
  assign controlled_buffer_4_out = and_2_out ? comparator_2_eq : 1'bz;  // Controlled_Buffer controlled_buffer_4
  Pull_Resistor pull_resistor_4 (.node(controlled_buffer_4_out));
  and and_2 (and_2_out, and_1_out, comparator_5_eq);
  Comparator #(.width(2)) comparator_5 (.a(2'b10), .b(MGRFwdst), .eq(comparator_5_eq));  // open: gt, lt
  Comparator #(.width(5)) comparator_6 (.a(Ewreg), .b(Drreg1), .eq(comparator_6_eq));  // open: gt, lt
  Comparator #(.width(5)) comparator_7 (.a(Ewreg), .b(Drreg2), .eq(comparator_7_eq));  // open: gt, lt
  Comparator #(.width(5)) comparator_8 (.a(Ewreg), .b({5{1'b0}}), .eq(comparator_8_eq));  // open: gt, lt
  Comparator #(.width(2)) comparator_9 (.a(2'b00), .b(Etnew), .eq(comparator_9_eq));  // open: gt, lt
  and and_3 (and_3_out, comparator_9_eq, ~comparator_8_eq, EGRFwen);  // AND_Gate
  assign controlled_buffer_5_out = and_4_out ? comparator_6_eq : 1'bz;  // Controlled_Buffer controlled_buffer_5
  assign controlled_buffer_6_out = and_4_out ? comparator_7_eq : 1'bz;  // Controlled_Buffer controlled_buffer_6
  and and_4 (and_4_out, and_3_out, comparator_10_eq);
  Comparator #(.width(2)) comparator_10 (.a(2'b10), .b(EGRFwdst), .eq(comparator_10_eq));  // open: gt, lt
  Pull_Resistor pull_resistor_5 (.node(controlled_buffer_5_out));
  Pull_Resistor pull_resistor_6 (.node(controlled_buffer_6_out));
  Priority_Encoder #(.select(2)) priority_encoder_1 (
    .in0(1'b1), .in1(controlled_buffer_1_out), .in2(controlled_buffer_3_out), .in3(controlled_buffer_5_out),
    .out(fw1));  // open: gs, en_out, en_in
  Priority_Encoder #(.select(2)) priority_encoder_2 (
    .in0(1'b1), .in1(pull_resistor_2_node), .in2(controlled_buffer_4_out), .in3(controlled_buffer_6_out),
    .out(fw2));  // open: gs, en_out, en_in
endmodule

module EFWCtrl (
  input  [1:0] MGRFwdst,
  input  [1:0] WGRFwdst,
  input  [4:0] Erreg1,
  input  [4:0] Erreg2,
  input  [4:0] Mwreg,
  input  [4:0] Wwreg,
  input  [1:0] Mtnew,
  input  [1:0] Wtnew,
  input  MGRFwen,
  input  WGRFwen,
  output [2:0] fw1,
  output [2:0] fw2
);

  wire and_1_out, and_2_out, comparator_1_eq, comparator_2_eq, comparator_3_eq, comparator_4_eq,
       comparator_5_eq, comparator_6_eq, comparator_7_eq, comparator_8_eq, comparator_9_eq, comparator_10_eq;
  wire [1:0] controlled_buffer_3_out, pull_resistor_4_node;

  Comparator #(.width(2)) comparator_1 (.a(2'b10), .b(MGRFwdst), .eq(comparator_1_eq));  // open: gt, lt
  Comparator #(.width(2)) comparator_2 (.a(2'b10), .b(WGRFwdst), .eq(comparator_2_eq));  // open: gt, lt
  Comparator #(.width(5)) comparator_3 (.a(Erreg1), .b(Mwreg), .eq(comparator_3_eq));  // open: gt, lt
  Comparator #(.width(5)) comparator_4 (.a(Erreg2), .b(Mwreg), .eq(comparator_4_eq));  // open: gt, lt
  Comparator #(.width(5)) comparator_5 (.a(Mwreg), .b({5{1'b0}}), .eq(comparator_5_eq));  // open: gt, lt
  Comparator #(.width(2)) comparator_6 (.a(Mtnew), .b(2'b00), .eq(comparator_6_eq));  // open: gt, lt
  assign controlled_buffer_3_out[1] = and_1_out ? comparator_3_eq : 1'bz;  // Controlled_Buffer controlled_buffer_1
  assign pull_resistor_4_node[1] = and_1_out ? comparator_4_eq : 1'bz;  // Controlled_Buffer controlled_buffer_2
  and and_1 (and_1_out, ~comparator_5_eq, comparator_6_eq, MGRFwen);  // AND_Gate
  Pull_Resistor pull_resistor_1 (.node(controlled_buffer_3_out[1]));
  Pull_Resistor pull_resistor_2 (.node(pull_resistor_4_node[1]));
  Comparator #(.width(5)) comparator_7 (.a(Erreg1), .b(Wwreg), .eq(comparator_7_eq));  // open: gt, lt
  Comparator #(.width(5)) comparator_8 (.a(Erreg2), .b(Wwreg), .eq(comparator_8_eq));  // open: gt, lt
  Comparator #(.width(5)) comparator_9 (.a(Wwreg), .b({5{1'b0}}), .eq(comparator_9_eq));  // open: gt, lt
  Comparator #(.width(2)) comparator_10 (.a(Wtnew), .b(2'b00), .eq(comparator_10_eq));  // open: gt, lt
  assign controlled_buffer_3_out[0] = and_2_out ? comparator_7_eq : 1'bz;  // Controlled_Buffer controlled_buffer_3
  Pull_Resistor pull_resistor_3 (.node(controlled_buffer_3_out[0]));
  Pull_Resistor pull_resistor_4 (.node(pull_resistor_4_node[0]));
  assign pull_resistor_4_node[0] = and_2_out ? comparator_8_eq : 1'bz;  // Controlled_Buffer controlled_buffer_4
  and and_2 (and_2_out, ~comparator_9_eq, comparator_10_eq, WGRFwen);  // AND_Gate
  Multiplexer #(.select(2), .enable("false")) multiplexer_1 (
    .in0(1'b0), .in1(comparator_2_eq), .in2(comparator_1_eq), .in3(comparator_1_eq), .out(fw2[2]),
    .sel(pull_resistor_4_node));
  Multiplexer #(.select(2), .enable("false")) multiplexer_2 (
    .in0(1'b0), .in1(comparator_2_eq), .in2(comparator_1_eq), .in3(comparator_1_eq), .out(fw1[2]),
    .sel(controlled_buffer_3_out));
  Priority_Encoder #(.select(2)) priority_encoder_1 (
    .in0(1'b1), .in1(controlled_buffer_3_out[0]), .in2(controlled_buffer_3_out[1]), .out(fw1[1:0]));  // open: in3, gs, en_out, en_in
  Priority_Encoder #(.select(2)) priority_encoder_2 (
    .in0(1'b1), .in1(pull_resistor_4_node[0]), .in2(pull_resistor_4_node[1]), .out(fw2[1:0]));  // open: in3, gs, en_out, en_in
endmodule

module SFWCtrl (
  input  [4:0] Mrreg2,
  input  [4:0] Wwreg,
  input  [1:0] Wtnew,
  input  WGRFwen,
  output fw2
);

  wire and_1_out, comparator_1_eq, comparator_2_eq, comparator_3_eq;

  Comparator #(.width(5)) comparator_1 (.a(Wwreg), .b({5{1'b0}}), .eq(comparator_1_eq));  // open: gt, lt
  Comparator #(.width(2)) comparator_2 (.a(Wtnew), .b(2'b00), .eq(comparator_2_eq));  // open: gt, lt
  and and_1 (and_1_out, ~comparator_1_eq, comparator_2_eq, WGRFwen);  // AND_Gate
  assign fw2 = and_1_out ? comparator_3_eq : 1'bz;  // Controlled_Buffer controlled_buffer_1
  Comparator #(.width(5)) comparator_3 (.a(Mrreg2), .b(Wwreg), .eq(comparator_3_eq));  // open: gt, lt
  Pull_Resistor pull_resistor_1 (.node(fw2));
endmodule

module StallCtrl (
  input  [4:0] Drs,
  input  [4:0] Drt,
  input  [4:0] Ewreg,
  input  [4:0] Mwreg,
  input  [1:0] Etnew,
  input  [1:0] Mtnew,
  input  EGRFwen,
  input  MGRFwen,
  input  [5:0] funct,
  input  [5:0] opcode,
  output stall
);

  wire and_1_out, and_2_out, and_3_out, and_4_out, Branch_out, comparator_1_eq, comparator_2_eq,
       comparator_3_eq, comparator_4_gt, comparator_5_eq, comparator_6_eq, comparator_7_eq, comparator_8_gt,
       comparator_9_eq, controlled_buffer_2_out, controlled_buffer_3_out, controlled_buffer_4_out,
       controlled_buffer_6_out, decoder_1_out0, decoder_1_out1, decoder_1_out4, decoder_1_out5,
       decoder_2_out0, decoder_2_out4, decoder_2_out5, decoder_2_out6, decoder_2_out7, JR_out, or_1_out,
       or_2_out, or_3_out, pull_resistor_1_node, pull_resistor_5_node, pull_resistor_7_node,
       pull_resistor_8_node, R_type_out;
  wire [1:0] priority_encoder_1_out;
  wire [2:0] bitselector_1_out, bitselector_2_out;

  BitSelector #(.width(6), .group(3)) bitselector_1 (.in(opcode), .out(bitselector_1_out), .sel(1'b0));
  BitSelector #(.width(6), .group(3)) bitselector_2 (.in(opcode), .out(bitselector_2_out), .sel(1'b1));
  Decoder #(.select(3), .disabled(0), .enable("false")) decoder_1 (
    .out0(decoder_1_out0), .out1(decoder_1_out1), .out4(decoder_1_out4), .out5(decoder_1_out5),
    .sel(bitselector_2_out));  // open: out2, out3, out6, out7
  Comparator #(.width(5)) comparator_1 (.a(Drs), .b(Ewreg), .eq(comparator_1_eq));  // open: gt, lt
  Comparator #(.width(5)) comparator_2 (.a(Drt), .b(Ewreg), .eq(comparator_2_eq));  // open: gt, lt
  Comparator #(.width(5)) comparator_3 (.a(Ewreg), .b({5{1'b0}}), .eq(comparator_3_eq));  // open: gt, lt
  Comparator #(.width(2), .mode("unsigned")) comparator_4 (
    .a(Etnew), .b(priority_encoder_1_out), .gt(comparator_4_gt));  // open: eq, lt
  Pull_Resistor pull_resistor_1 (.node(pull_resistor_1_node));
  assign pull_resistor_1_node = and_1_out ? comparator_1_eq : 1'bz;  // Controlled_Buffer controlled_buffer_1
  assign controlled_buffer_2_out = and_1_out ? comparator_2_eq : 1'bz;  // Controlled_Buffer controlled_buffer_2
  Pull_Resistor pull_resistor_2 (.node(controlled_buffer_2_out));
  and and_1 (and_1_out, comparator_4_gt, ~comparator_3_eq, EGRFwen);  // AND_Gate
  Decoder #(.select(3), .disabled(0)) decoder_2 (
    .out0(decoder_2_out0), .out4(decoder_2_out4), .out5(decoder_2_out5), .out6(decoder_2_out6),
    .out7(decoder_2_out7), .sel(bitselector_1_out), .en(decoder_1_out0));  // open: out1, out2, out3
  or or_1 (or_1_out, decoder_2_out4, decoder_2_out5, decoder_2_out6, decoder_2_out7);
  Decoder #(.select(3), .disabled(0)) decoder_3 (
    .sel(bitselector_1_out), .en(decoder_1_out1));  // open: out0, out1, out2, out3, out4, out5, out6, out7
  Comparator #(.width(5)) comparator_5 (.a(Drs), .b(Mwreg), .eq(comparator_5_eq));  // open: gt, lt
  assign controlled_buffer_3_out = and_2_out ? comparator_5_eq : 1'bz;  // Controlled_Buffer controlled_buffer_3
  Comparator #(.width(5)) comparator_6 (.a(Drt), .b(Mwreg), .eq(comparator_6_eq));  // open: gt, lt
  assign controlled_buffer_4_out = and_2_out ? comparator_6_eq : 1'bz;  // Controlled_Buffer controlled_buffer_4
  Comparator #(.width(5)) comparator_7 (.a(Mwreg), .b({5{1'b0}}), .eq(comparator_7_eq));  // open: gt, lt
  and and_2 (and_2_out, comparator_8_gt, ~comparator_7_eq, MGRFwen);  // AND_Gate
  Comparator #(.width(2), .mode("unsigned")) comparator_8 (
    .a(Mtnew), .b(priority_encoder_1_out), .gt(comparator_8_gt));  // open: eq, lt
  and and_3 (and_3_out, ~and_4_out, decoder_2_out0);  // AND_Gate
  Pull_Resistor pull_resistor_3 (.node(controlled_buffer_3_out));
  Pull_Resistor pull_resistor_4 (.node(controlled_buffer_4_out));
  Decoder #(.select(3), .disabled(0)) decoder_4 (
    .sel(bitselector_1_out), .en(decoder_1_out4));  // open: out0, out1, out2, out3, out4, out5, out6, out7
  Decoder #(.select(3), .disabled(0)) decoder_5 (
    .sel(bitselector_1_out), .en(decoder_1_out5));  // open: out0, out1, out2, out3, out4, out5, out6, out7
  Comparator #(.width(6)) comparator_9 (.a(funct), .b(6'b001000), .eq(comparator_9_eq));  // open: gt, lt
  or Branch (Branch_out, controlled_buffer_2_out, pull_resistor_1_node, controlled_buffer_4_out, controlled_buffer_3_out);
  Pull_Resistor pull_resistor_5 (.node(pull_resistor_5_node));
  assign pull_resistor_5_node = or_1_out ? Branch_out : 1'bz;  // Controlled_Buffer controlled_buffer_5
  or JR (JR_out, pull_resistor_1_node, controlled_buffer_3_out);
  assign controlled_buffer_6_out = and_4_out ? JR_out : 1'bz;  // Controlled_Buffer controlled_buffer_6
  or R_type (R_type_out, controlled_buffer_2_out, pull_resistor_1_node);
  or or_2 (or_2_out, decoder_1_out1, decoder_1_out4, decoder_1_out5);
  or or_3 (or_3_out, and_3_out, decoder_1_out1, decoder_1_out4, decoder_1_out5);
  and and_4 (and_4_out, comparator_9_eq, decoder_2_out0);
  Pull_Resistor pull_resistor_6 (.node(controlled_buffer_6_out));
  Pull_Resistor pull_resistor_7 (.node(pull_resistor_7_node));
  assign pull_resistor_7_node = decoder_2_out0 ? R_type_out : 1'bz;  // Controlled_Buffer controlled_buffer_7
  Pull_Resistor pull_resistor_8 (.node(pull_resistor_8_node));
  assign pull_resistor_8_node = or_2_out ? pull_resistor_1_node : 1'bz;  // Controlled_Buffer controlled_buffer_8
  Priority_Encoder #(.select(2)) priority_encoder_1 (
    .in0(1'b1), .in1(or_3_out), .out(priority_encoder_1_out));  // open: in2, in3, gs, en_out, en_in
  or or_4 (stall, pull_resistor_5_node, controlled_buffer_6_out, pull_resistor_7_node, pull_resistor_8_node);

  // Notes on the sheet:
  //   There's a bug.
  //   ers
  //   ert
  //   R,J,B
  //   Imm
  //   Load
  //   Users:
  //   I&L&S
  //   Store
  //   special for JR & JAL
  //   JR
endmodule

module MUDV (
  input  [1:0] mdop,
  input  start,
  input  clk,
  input  [31:0] opa,
  input  [31:0] opb,
  input  [1:0] write_en,
  output busy,
  output [31:0] lo,
  output [31:0] hi
);

  wire and_1_out, comparator_1_eq, comparator_2_eq, or_1_out;
  wire [1:0] mdop_q;
  wire [3:0] counter_1_q, multiplexer_1_out;
  wire [31:0] divider_1_out, divider_1_rem, multiplexer_2_out, multiplexer_3_out, multiplexer_4_out,
       multiplexer_5_out, multiplier_1_cout, multiplier_1_out, opa_q, opb_q;

  Multiplexer #(.select(2), .width(4)) multiplexer_1 (
    .in0(4'b0000), .in1(4'b0101), .in2(4'b1010), .out(multiplexer_1_out), .sel(mdop), .en(start));  // open: in3
  Register #(.width(2)) u_mdop (.D(mdop), .en(start), .Q(mdop_q), .clk(clk));  // open: clr
  Register #(.width(32)) u_opa (.D(opa), .en(start), .Q(opa_q), .clk(clk));  // open: clr
  Register #(.width(32)) u_opb (.D(opb), .en(start), .Q(opb_q), .clk(clk));  // open: clr
  or or_1 (or_1_out, start, ~comparator_1_eq);  // OR_Gate
  and and_1 (and_1_out, ~start, ~comparator_1_eq);  // AND_Gate
  Multiplier #(.width(32)) multiplier_1 (
    .a(opa_q), .b(opb_q), .out(multiplier_1_out), .cout(multiplier_1_cout));  // open: cin
  Divider #(.width(32)) divider_1 (.a(opa_q), .b(opb_q), .out(divider_1_out), .rem(divider_1_rem));  // open: upper
  Counter #(.width(4), .max('hf), .ongoal("stay")) counter_1 (
    .load(or_1_out), .D(multiplexer_1_out), .count(and_1_out), .Q(counter_1_q), .clk(clk));  // open: carry, clr
  Multiplexer #(.select(2), .width(32)) multiplexer_2 (
    .in1(multiplier_1_out), .in2(divider_1_out), .out(multiplexer_2_out), .sel(mdop_q), .en(comparator_2_eq));  // open: in0, in3
  Multiplexer #(.select(2), .width(32)) multiplexer_3 (
    .in1(multiplier_1_cout), .in2(divider_1_rem), .out(multiplexer_3_out), .sel(mdop_q), .en(comparator_2_eq));  // open: in0, in3
  Comparator #(.width(4)) comparator_1 (.a(counter_1_q), .b(4'b0000), .gt(busy), .eq(comparator_1_eq));  // open: lt
  Comparator #(.width(4)) comparator_2 (.a(counter_1_q), .b(4'b0001), .eq(comparator_2_eq));  // open: gt, lt
  Multiplexer #(.width(32), .enable("false")) multiplexer_4 (
    .in0(multiplexer_2_out), .in1(opa_q), .out(multiplexer_4_out), .sel(write_en[0]));
  Multiplexer #(.width(32), .enable("false")) multiplexer_5 (
    .in0(multiplexer_3_out), .in1(opa_q), .out(multiplexer_5_out), .sel(write_en[1]));
  Register #(.width(32)) u_LO (.D(multiplexer_4_out), .Q(lo), .clk(clk));  // open: en, clr
  Register #(.width(32)) u_HI (.D(multiplexer_5_out), .Q(hi), .clk(clk));  // open: en, clr
endmodule
