// Logisim project processor_single_cycle.circ as structural Verilog: 9 circuits, main circuit Processor
module Processor (
  input  Reset,
  output halt,
  output [31:0] out_3,
  output [31:0] out_4,
  output [31:0] out_5
);

  wire clock_1_out, grf_1_zero, mainctrl_1_aluien, mainctrl_1_alushsrc, mainctrl_1_extsign, MemWrite,
       RegWrite;
  wire [0:0] mainctrl_1_dmwrstate;
  wire [1:0] mainctrl_1_grfwdatsrc, mainctrl_1_grfwdst, mainctrl_1_pcsrc;
  wire [3:0] aluctrl_1_aluop, bitselector_1_out, mainctrl_1_alufn;
  wire [4:0] fieldsel_1_rd, fieldsel_1_rs, fieldsel_1_rt, fieldsel_1_shamt, multiplexer_7_out, RegAddr;
  wire [5:0] fieldsel_1_funct, fieldsel_1_opcode;
  wire [15:0] fieldsel_1_imm;
  wire [25:0] fieldsel_1_instr_ind;
  wire [31:0] adder_1_out, adder_2_out, bit_extender_1_out, bit_extender_2_out, bit_extender_3_out,
       datamem_1_rdat, grf_1_rdat1, instrmem_1_instr, MemAddr, MemData, multiplexer_5_out, multiplexer_6_out,
       multiplexer_8_out, npc, RegData, shifter_1_out;

  Clock clock_1 (.out(clock_1_out));
  Multiplexer #(.select(2), .width(32), .enable("false")) multiplexer_1 (
    .in0(adder_1_out), .in1(multiplexer_6_out), .in2({bitselector_1_out, fieldsel_1_instr_ind, 2'b00}),
    .in3(grf_1_rdat1), .out(npc), .sel(mainctrl_1_pcsrc));
  // Probe on out_5
  PC pc_1 (.npc(npc), .pc(out_5), .RST(Reset), .CLK(clock_1_out));
  Counter #(.width(32), .max('h4), .ongoal("stay")) counter_1 (
    .carry(halt), .clk(clock_1_out));  // open: load, D, count, Q, clr
  assign bit_extender_1_out = {{27{1'b0}}, RegAddr};  // Bit_Extender bit_extender_1
  Adder #(.width(32)) adder_1 (.a(out_5), .b(32'h4), .out(adder_1_out));  // open: cin, cout
  InstrMem instrmem_1 (.pc(out_5), .instr(instrmem_1_instr));
  Multiplexer #(.select(2), .width(32), .enable("false")) multiplexer_2 (
    .in0({32{1'b0}}), .in1(MemAddr), .in2(bit_extender_1_out), .out(out_3), .sel({RegWrite, MemWrite}));  // open: in3
  Multiplexer #(.select(2), .width(32), .enable("false")) multiplexer_3 (
    .in0(npc), .in1(MemData), .in2(RegData), .out(out_4), .sel({RegWrite, MemWrite}));  // open: in3
  Pull_Resistor pull_resistor_1 (.node(out_4));
  Pull_Resistor pull_resistor_2 (.node(out_3));
  FieldSel fieldsel_1 (
    .instr(instrmem_1_instr), .shamt(fieldsel_1_shamt), .rs(fieldsel_1_rs), .rt(fieldsel_1_rt),
    .rd(fieldsel_1_rd), .imm(fieldsel_1_imm), .opcode(fieldsel_1_opcode), .funct(fieldsel_1_funct),
    .instr_ind(fieldsel_1_instr_ind));
  MainCtrl mainctrl_1 (
    .opcode(fieldsel_1_opcode), .GRFwen(RegWrite), .GRFwdst(mainctrl_1_grfwdst),
    .GRFwdatsrc(mainctrl_1_grfwdatsrc), .ALUfn(mainctrl_1_alufn), .ALUshsrc(mainctrl_1_alushsrc),
    .ALUien(mainctrl_1_aluien), .EXTsign(mainctrl_1_extsign),
    .DMwrstate({MemWrite, mainctrl_1_dmwrstate[0]}), .funct(fieldsel_1_funct), .PCsrc(mainctrl_1_pcsrc));
  assign bit_extender_2_out = {{16{1'b0}}, fieldsel_1_imm};  // Bit_Extender bit_extender_2
  assign bit_extender_3_out = {{16{fieldsel_1_imm[15]}}, fieldsel_1_imm};  // Bit_Extender bit_extender_3
  ALUCtrl aluctrl_1 (.funct(fieldsel_1_funct), .ALUop(aluctrl_1_aluop), .ALUfn(mainctrl_1_alufn));
  Shifter #(.width(32)) shifter_1 (.in(bit_extender_3_out), .\dist (5'b00010), .out(shifter_1_out));
  BitSelector #(.width(32), .group(4)) bitselector_1 (.in(out_5), .out(bitselector_1_out), .sel(3'b111));
  Multiplexer #(.select(2), .width(5), .enable("false")) multiplexer_4 (
    .in0(fieldsel_1_rt), .in1(fieldsel_1_rd), .in2({5{1'b1}}), .out(RegAddr), .sel(mainctrl_1_grfwdst));  // open: in3
  Multiplexer #(.width(32), .enable("false")) multiplexer_5 (
    .in0(bit_extender_2_out), .in1(bit_extender_3_out), .out(multiplexer_5_out), .sel(mainctrl_1_extsign));
  Adder #(.width(32)) adder_2 (.a(adder_1_out), .b(shifter_1_out), .out(adder_2_out));  // open: cin, cout
  Multiplexer #(.width(32), .enable("false")) multiplexer_6 (
    .in0(adder_1_out), .in1(adder_2_out), .out(multiplexer_6_out), .sel(grf_1_zero));
  GRF grf_1 (
    .radd1(fieldsel_1_rs), .radd2(fieldsel_1_rt), .wadd(RegAddr), .wdat(RegData), .rdat1(grf_1_rdat1),
    .rdat2(MemData), .CLK(clock_1_out), .RST(Reset), .GRFwrite_en(RegWrite), .zero(grf_1_zero));
  Multiplexer #(.width(5), .enable("false")) multiplexer_7 (
    .in0(fieldsel_1_shamt), .in1(5'b10000), .out(multiplexer_7_out), .sel(mainctrl_1_alushsrc));
  Multiplexer #(.width(32), .enable("false")) multiplexer_8 (
    .in0(MemData), .in1(multiplexer_5_out), .out(multiplexer_8_out), .sel(mainctrl_1_aluien));
  ALU alu_1 (
    .op1(grf_1_rdat1), .op2(multiplexer_8_out), .res(MemAddr), .ALUop(aluctrl_1_aluop),
    .shamt(multiplexer_7_out));
  DataMem datamem_1 (
    .addr(MemAddr), .wdat(MemData), .rdat(datamem_1_rdat), .CLK(clock_1_out), .DMwrite(MemWrite),
    .RST(Reset), .DMread(mainctrl_1_dmwrstate[0]));
  Multiplexer #(.select(2), .width(32), .enable("false")) multiplexer_9 (
    .in0(MemAddr), .in1(datamem_1_rdat), .in2(adder_1_out), .out(RegData), .sel(mainctrl_1_grfwdatsrc));  // open: in3

  // Other names for the same wires on the sheet: pc[31:0] = out_5

  // Notes on the sheet:
  //   TestBench
  //   pc+4
  //   GRFwen
  //   GRFwrdst
  //   GRFwdsrc
  //   ALUshsrc
  //   ALUien
  //   EXTsign
  //   PCsrc
  //   DMstate
  //   pc+4+offset
  //   jump add
  //   jump to reg
endmodule

module PC (
  input  [31:0] npc,
  input  RST,
  input  CLK,
  output [31:0] pc
);

  wire [31:0] multiplexer_1_out, register_1_q, subtractor_1_out;

  // Probe on npc
  Subtractor #(.width(32)) subtractor_1 (.a(npc), .b(32'h3000), .out(subtractor_1_out));  // open: bin, bout
  Multiplexer #(.width(32), .enable("false")) multiplexer_1 (
    .in0(subtractor_1_out), .in1({32{1'b0}}), .out(multiplexer_1_out), .sel(RST));
  Register #(.width(32)) register_1 (.D(multiplexer_1_out), .Q(register_1_q), .clk(CLK));  // open: en, clr
  // Probe on pc
  Adder #(.width(32)) adder_1 (.a(register_1_q), .b(32'h3000), .out(pc));  // open: cin, cout
endmodule

module InstrMem (
  input  [31:0] pc,
  output [31:0] instr
);

  wire [11:0] bitselector_1_out;
  wire [31:0] shifter_1_out, subtractor_1_out;

  // Probe on subtractor_1_out
  Subtractor #(.width(32)) subtractor_1 (.a(pc), .b(32'h3000), .out(subtractor_1_out));  // open: bin, bout
  Shifter #(.width(32), .shift("lr")) shifter_1 (.in(subtractor_1_out), .\dist (5'b00010), .out(shifter_1_out));
  BitSelector #(.width(32), .group(12)) bitselector_1 (.in(shifter_1_out), .out(bitselector_1_out), .sel(2'b00));
  ROM #(.addrWidth(12), .dataWidth(32)) rom_1 (.addr(bitselector_1_out), .data(instr));  // open: sel
  // Probe on instr

  // Notes on the sheet:
  //   contents of rom_1 (hex, n*v repeats v):
  //   340115bb ac010000 34012bd6 ac010000 8c000000
endmodule

module FieldSel (
  input  [31:0] instr,
  output [4:0] shamt,
  output [4:0] rs,
  output [4:0] rt,
  output [4:0] rd,
  output [15:0] imm,
  output [25:0] instr_ind,
  output [5:0] opcode,
  output [5:0] funct
);


  assign funct = instr[5:0];
  assign imm = instr[15:0];
  assign instr_ind = instr[25:0];
  assign opcode = instr[31:26];
  assign rd = instr[15:11];
  assign rs = instr[25:21];
  assign rt = instr[20:16];
  assign shamt = instr[10:6];
endmodule

module GRF (
  input  [4:0] radd1,
  input  [4:0] radd2,
  input  [4:0] wadd,
  input  [31:0] wdat,
  input  GRFwrite_en,
  input  CLK,
  input  RST,
  output [31:0] rdat1,
  output [31:0] rdat2,
  output zero
);

  wire RST_t;
  wire [31:0] multiplexer_3_out, multiplexer_4_out, r0, r0o, r1, r1o, r2, r2o, r3, r3o, r4, r4o, r5, r5o, r6,
       r6o, r7, r7o, r8, r8o, r9, r9o, r10, r10o, r11, r11o, r12, r12o, r13, r13o, r14, r14o, r15, r15o, r16,
       r16o, r17, r17o, r18, r18o, r19, r19o, r20, r20o, r21, r21o, r22, r22o, r23, r23o, r24, r24o, r25,
       r25o, r26, r26o, r27, r27o, r28, r28o, r29, r29o, r30, r30o, r31, r31o;

  Multiplexer #(.select(5), .width(32), .enable("false")) multiplexer_1 (
    .in0(r0o), .in1(r1o), .in2(r2o), .in3(r3o), .in4(r4o), .in5(r5o), .in6(r6o), .in7(r7o), .in8(r8o),
    .in9(r9o), .in10(r10o), .in11(r11o), .in12(r12o), .in13(r13o), .in14(r14o), .in15(r15o), .in16(r16o),
    .in17(r17o), .in18(r18o), .in19(r19o), .in20(r20o), .in21(r21o), .in22(r22o), .in23(r23o), .in24(r24o),
    .in25(r25o), .in26(r26o), .in27(r27o), .in28(r28o), .in29(r29o), .in30(r30o), .in31(r31o), .out(rdat1),
    .sel(radd1));
  D_Flip_Flop d_ff_1 (.clk(CLK), .D(RST), .Q(RST_t));  // open: Qn, preset, en, reset
  Multiplexer #(.select(5), .width(32), .enable("false")) multiplexer_2 (
    .in0(r0o), .in1(r1o), .in2(r2o), .in3(r3o), .in4(r4o), .in5(r5o), .in6(r6o), .in7(r7o), .in8(r8o),
    .in9(r9o), .in10(r10o), .in11(r11o), .in12(r12o), .in13(r13o), .in14(r14o), .in15(r15o), .in16(r16o),
    .in17(r17o), .in18(r18o), .in19(r19o), .in20(r20o), .in21(r21o), .in22(r22o), .in23(r23o), .in24(r24o),
    .in25(r25o), .in26(r26o), .in27(r27o), .in28(r28o), .in29(r29o), .in30(r30o), .in31(r31o), .out(rdat2),
    .sel(radd2));
  Register #(.width(32)) register_1 (.D({32{1'b0}}), .en(1'b1), .Q(r0o), .clk(CLK), .clr(RST_t));
  Register #(.width(32)) register_2 (.D(r8), .en(1'b1), .Q(r8o), .clk(CLK), .clr(RST_t));
  Register #(.width(32)) register_3 (.D(r16), .en(1'b1), .Q(r16o), .clk(CLK), .clr(RST_t));
  Register #(.width(32)) register_4 (.D(r24), .en(1'b1), .Q(r24o), .clk(CLK), .clr(RST_t));
  Register #(.width(32)) register_5 (.D(r1), .en(1'b1), .Q(r1o), .clk(CLK), .clr(RST_t));
  Register #(.width(32)) register_6 (.D(r9), .en(1'b1), .Q(r9o), .clk(CLK), .clr(RST_t));
  Register #(.width(32)) register_7 (.D(r17), .en(1'b1), .Q(r17o), .clk(CLK), .clr(RST_t));
  Register #(.width(32)) register_8 (.D(r25), .en(1'b1), .Q(r25o), .clk(CLK), .clr(RST_t));
  Multiplexer #(.select(5), .width(32), .enable("false")) multiplexer_3 (
    .in0(r0o), .in1(r1o), .in2(r2o), .in3(r3o), .in4(r4o), .in5(r5o), .in6(r6o), .in7(r7o), .in8(r8o),
    .in9(r9o), .in10(r10o), .in11(r11o), .in12(r12o), .in13(r13o), .in14(r14o), .in15(r15o), .in16(r16o),
    .in17(r17o), .in18(r18o), .in19(r19o), .in20(r20o), .in21(r21o), .in22(r22o), .in23(r23o), .in24(r24o),
    .in25(r25o), .in26(r26o), .in27(r27o), .in28(r28o), .in29(r29o), .in30(r30o), .in31(r31o),
    .out(multiplexer_3_out), .sel(wadd));
  Register #(.width(32)) register_9 (.D(r2), .en(1'b1), .Q(r2o), .clk(CLK), .clr(RST_t));
  Register #(.width(32)) register_10 (.D(r10), .en(1'b1), .Q(r10o), .clk(CLK), .clr(RST_t));
  Register #(.width(32)) register_11 (.D(r18), .en(1'b1), .Q(r18o), .clk(CLK), .clr(RST_t));
  Register #(.width(32)) register_12 (.D(r26), .en(1'b1), .Q(r26o), .clk(CLK), .clr(RST_t));
  Demultiplexer #(.select(5), .width(32), .tristate("true"), .enable("false")) demultiplexer_1 (
    .out0(r0), .out1(r1), .out2(r2), .out3(r3), .out4(r4), .out5(r5), .out6(r6), .out7(r7), .out8(r8),
    .out9(r9), .out10(r10), .out11(r11), .out12(r12), .out13(r13), .out14(r14), .out15(r15), .out16(r16),
    .out17(r17), .out18(r18), .out19(r19), .out20(r20), .out21(r21), .out22(r22), .out23(r23), .out24(r24),
    .out25(r25), .out26(r26), .out27(r27), .out28(r28), .out29(r29), .out30(r30), .out31(r31),
    .in(multiplexer_4_out), .sel(wadd));
  Multiplexer #(.width(32), .enable("false")) multiplexer_4 (
    .in0(multiplexer_3_out), .in1(wdat), .out(multiplexer_4_out), .sel(GRFwrite_en));
  Register #(.width(32)) register_13 (.D(r3), .en(1'b1), .Q(r3o), .clk(CLK), .clr(RST_t));
  Register #(.width(32)) register_14 (.D(r11), .en(1'b1), .Q(r11o), .clk(CLK), .clr(RST_t));
  Register #(.width(32)) register_15 (.D(r19), .en(1'b1), .Q(r19o), .clk(CLK), .clr(RST_t));
  Register #(.width(32)) register_16 (.D(r27), .en(1'b1), .Q(r27o), .clk(CLK), .clr(RST_t));
  Register #(.width(32)) register_17 (.D(r4), .en(1'b1), .Q(r4o), .clk(CLK), .clr(RST_t));
  Register #(.width(32)) register_18 (.D(r12), .en(1'b1), .Q(r12o), .clk(CLK), .clr(RST_t));
  Register #(.width(32)) register_19 (.D(r20), .en(1'b1), .Q(r20o), .clk(CLK), .clr(RST_t));
  Register #(.width(32)) register_20 (.D(r28), .en(1'b1), .Q(r28o), .clk(CLK), .clr(RST_t));
  Register #(.width(32)) register_21 (.D(r5), .en(1'b1), .Q(r5o), .clk(CLK), .clr(RST_t));
  Register #(.width(32)) register_22 (.D(r13), .en(1'b1), .Q(r13o), .clk(CLK), .clr(RST_t));
  Register #(.width(32)) register_23 (.D(r21), .en(1'b1), .Q(r21o), .clk(CLK), .clr(RST_t));
  Register #(.width(32)) register_24 (.D(r29), .en(1'b1), .Q(r29o), .clk(CLK), .clr(RST_t));
  Register #(.width(32)) register_25 (.D(r6), .en(1'b1), .Q(r6o), .clk(CLK), .clr(RST_t));
  Register #(.width(32)) register_26 (.D(r14), .en(1'b1), .Q(r14o), .clk(CLK), .clr(RST_t));
  Register #(.width(32)) register_27 (.D(r22), .en(1'b1), .Q(r22o), .clk(CLK), .clr(RST_t));
  Register #(.width(32)) register_28 (.D(r30), .en(1'b1), .Q(r30o), .clk(CLK), .clr(RST_t));
  Comparator #(.width(32)) comparator_1 (.a(rdat1), .b(rdat2), .eq(zero));  // open: gt, lt
  Register #(.width(32)) register_29 (.D(r7), .en(1'b1), .Q(r7o), .clk(CLK), .clr(RST_t));
  Register #(.width(32)) register_30 (.D(r15), .en(1'b1), .Q(r15o), .clk(CLK), .clr(RST_t));
  Register #(.width(32)) register_31 (.D(r23), .en(1'b1), .Q(r23o), .clk(CLK), .clr(RST_t));
  Register #(.width(32)) register_32 (.D(r31), .en(1'b1), .Q(r31o), .clk(CLK), .clr(RST_t));

  // Other names for the same wires on the sheet: IN[31:0] = wdat; read1[4:0] = radd1; read2[4:0] = radd2;
  //   read_data1[31:0] = rdat1; read_data2[31:0] = rdat2; WEN = GRFwrite_en; write[4:0] = wadd

  // Notes on the sheet:
  //   interfaces
  //   output
  //   registers
  //   input
endmodule

module ALU (
  input  [3:0] ALUop,
  input  [31:0] op1,
  input  [31:0] op2,
  input  [4:0] shamt,
  output [31:0] res
);

  wire [31:0] adder_1_out, and_1_out, or_1_out, shifter_1_out, shifter_2_out, shifter_3_out, subtractor_1_out;

  Shifter #(.width(32)) shifter_1 (.in(op2), .\dist (shamt), .out(shifter_1_out));
  Shifter #(.width(32), .shift("lr")) shifter_2 (.in(op2), .\dist (shamt), .out(shifter_2_out));
  Shifter #(.width(32), .shift("ar")) shifter_3 (.in(op2), .\dist (shamt), .out(shifter_3_out));
  Adder #(.width(32)) adder_1 (.a(op1), .b(op2), .out(adder_1_out));  // open: cin, cout
  Subtractor #(.width(32)) subtractor_1 (.a(op1), .b(op2), .out(subtractor_1_out));  // open: bin, bout
  assign and_1_out = op1 & op2;  // AND_Gate and_1, 32 bits wide
  assign or_1_out = op1 | op2;  // OR_Gate or_1, 32 bits wide
  Multiplexer #(.select(4), .width(32), .enable("false")) multiplexer_1 (
    .in0(shifter_1_out), .in1(shifter_2_out), .in2(shifter_3_out), .in3(adder_1_out), .in4(subtractor_1_out),
    .in5(and_1_out), .in6(or_1_out), .out(res), .sel(ALUop));  // open: in7, in8, in9, in10, in11, in12, in13, in14, in15
endmodule

module DataMem (
  input  [31:0] addr,
  input  DMwrite,
  input  DMread,
  input  [31:0] wdat,
  input  CLK,
  input  RST,
  output [31:0] rdat
);

  wire d_ff_1_q;
  wire [11:0] bitselector_1_out;
  wire [31:0] shifter_1_out;

  Shifter #(.width(32), .shift("lr")) shifter_1 (.in(addr), .\dist (5'b00010), .out(shifter_1_out));
  BitSelector #(.width(32), .group(12)) bitselector_1 (.in(shifter_1_out), .out(bitselector_1_out), .sel(2'b00));
  RAM #(.addrWidth(12), .dataWidth(32), .bus("separate")) ram_1 (
    .addr(bitselector_1_out), .din(wdat), .data(rdat), .str(DMwrite), .clk(CLK), .ld(DMread), .clr(d_ff_1_q));  // open: sel
  D_Flip_Flop d_ff_1 (.clk(CLK), .D(RST), .Q(d_ff_1_q));  // open: Qn, preset, en, reset
endmodule

module ALUCtrl (
  input  [5:0] funct,
  input  [3:0] ALUfn,
  output [3:0] ALUop
);

  wire comparator_1_eq, comparator_2_eq, not_1_out;
  wire [1:0] bitselector_3_out;
  wire [2:0] bitselector_1_out, bitselector_2_out;
  wire [3:0] multiplexer_1_out, multiplexer_2_out, multiplexer_3_out, multiplexer_4_out;

  BitSelector #(.width(6), .group(3)) bitselector_1 (.in(funct), .out(bitselector_1_out), .sel(1'b1));
  BitSelector #(.width(6), .group(3)) bitselector_2 (.in(funct), .out(bitselector_2_out), .sel(1'b0));
  BitSelector #(.width(3), .group(2)) bitselector_3 (.in(bitselector_2_out), .out(bitselector_3_out), .sel(1'b0));
  Multiplexer #(.select(2), .width(4), .enable("false")) multiplexer_1 (
    .in0(4'b0000), .in2(4'b0001), .in3(4'b0010), .out(multiplexer_1_out), .sel(bitselector_3_out));  // open: in1
  Multiplexer #(.select(3), .width(4), .enable("false")) multiplexer_2 (
    .in0(4'b0011), .in2(4'b0100), .in4(4'b0101), .in5(4'b0110), .in6(4'b0111), .in7(4'b1000),
    .out(multiplexer_2_out), .sel(bitselector_2_out));  // open: in1, in3
  Multiplexer #(.select(3), .width(4), .enable("false")) multiplexer_3 (
    .in0(multiplexer_1_out), .in4(multiplexer_2_out), .in5(4'b1001), .out(multiplexer_3_out),
    .sel(bitselector_1_out));  // open: in1, in2, in3, in6, in7
  Pull_Resistor pull_resistor_1 (.node(ALUfn));
  Multiplexer #(.width(4), .enable("false")) multiplexer_4 (
    .in0(multiplexer_3_out), .in1(ALUfn), .out(multiplexer_4_out), .sel(not_1_out));
  not not_1 (not_1_out, comparator_1_eq);
  Comparator #(.width(4), .mode("unsigned")) comparator_1 (
    .a(ALUfn), .b(4'b0000), .eq(comparator_1_eq));  // open: gt, lt
  Comparator #(.width(4), .mode("unsigned")) comparator_2 (
    .a(ALUfn), .b(4'b1111), .eq(comparator_2_eq));  // open: gt, lt
  Multiplexer #(.width(4), .enable("false")) multiplexer_5 (
    .in0(multiplexer_4_out), .in1(4'b0000), .out(ALUop), .sel(comparator_2_eq));
endmodule

module MainCtrl (
  input  [5:0] funct,
  input  [5:0] opcode,
  output GRFwen,
  output [1:0] GRFwdst,
  output [1:0] GRFwdatsrc,
  output [3:0] ALUfn,
  output ALUshsrc,
  output ALUien,
  output EXTsign,
  output [1:0] PCsrc,
  output [1:0] DMwrstate
);

  wire and_1_out, and_2_out, and_3_out, and_4_out, and_5_out, bitselector_3_out, comparator_1_eq,
       decoder_1_out0, decoder_1_out1, decoder_1_out4, decoder_1_out5, decoder_2_out0, decoder_2_out1,
       decoder_2_out3, decoder_3_out4, decoder_3_out5, decoder_3_out6, not_2_out, or_1_out, or_2_out,
       or_3_out, or_5_out;
  wire [1:0] priority_encoder_4_out;
  wire [2:0] bitselector_1_out, bitselector_2_out;

  BitSelector #(.width(6), .group(3)) bitselector_1 (.in(opcode), .out(bitselector_1_out), .sel(1'b1));
  BitSelector #(.width(6), .group(3)) bitselector_2 (.in(opcode), .out(bitselector_2_out), .sel(1'b0));
  Decoder #(.select(3), .disabled(0), .enable("false")) decoder_1 (
    .out0(decoder_1_out0), .out1(decoder_1_out1), .out4(decoder_1_out4), .out5(decoder_1_out5),
    .sel(bitselector_1_out));  // open: out2, out3, out6, out7
  and and_1 (and_1_out, decoder_1_out0, ~or_1_out);  // AND_Gate
  BitSelector #(.width(3)) bitselector_3 (.in(bitselector_2_out), .out(bitselector_3_out), .sel(2'b10));
  or or_1 (or_1_out, decoder_2_out0, decoder_2_out1);
  and and_2 (and_2_out, and_1_out, bitselector_3_out);
  and and_3 (and_3_out, and_1_out, ~bitselector_3_out);  // AND_Gate
  Decoder #(.select(3), .disabled(0)) decoder_2 (
    .out0(decoder_2_out0), .out1(decoder_2_out1), .out3(decoder_2_out3), .sel(bitselector_2_out),
    .en(decoder_1_out0));  // open: out2, out4, out5, out6, out7
  Comparator #(.width(6)) comparator_1 (.a(funct), .b(6'b001000), .eq(comparator_1_eq));  // open: gt, lt
  Decoder #(.select(3), .disabled(0)) decoder_3 (
    .out4(decoder_3_out4), .out5(decoder_3_out5), .out6(decoder_3_out6), .out7(ALUshsrc),
    .sel(bitselector_2_out), .en(decoder_1_out1));  // open: out0, out1, out2, out3
  and and_4 (and_4_out, comparator_1_eq, decoder_2_out0);
  Decoder #(.select(3), .disabled(0)) decoder_4 (
    .sel(bitselector_2_out), .en(decoder_1_out4));  // open: out0, out1, out2, out3, out4, out5, out6, out7
  or or_2 (or_2_out, and_4_out, decoder_2_out3);
  Decoder #(.select(3), .disabled(0)) decoder_5 (
    .sel(bitselector_2_out), .en(decoder_1_out5));  // open: out0, out1, out2, out3, out4, out5, out6, out7
  or or_3 (or_3_out, decoder_1_out4, decoder_1_out5);
  or or_4 (ALUien, decoder_1_out5, decoder_1_out4, decoder_1_out1);
  or or_5 (or_5_out, decoder_3_out4, decoder_3_out5, decoder_3_out6);
  and and_5 (and_5_out, ~decoder_1_out5, ~and_1_out);  // AND_Gate
  Priority_Encoder #(.select(2)) priority_encoder_1 (
    .in0(1'b1), .in1(or_1_out), .in2(decoder_2_out3), .out(GRFwdst));  // open: in3, gs, en_out, en_in
  Priority_Encoder #(.select(2)) priority_encoder_2 (
    .in0(1'b1), .in1(decoder_1_out4), .in2(decoder_2_out3), .out(GRFwdatsrc));  // open: in3, gs, en_out, en_in
  Priority_Encoder #(.select(4)) priority_encoder_3 (
    .in0(1'b1), .in3(or_3_out), .in4(and_1_out), .in6(decoder_3_out5), .in15(ALUshsrc), .out(ALUfn));  // open: in1, in2, in5, in7, in8, in9, in10, in11, in12, in13, in14, gs, en_out, en_in
  not not_1 (EXTsign, or_5_out);
  Priority_Encoder #(.select(2)) priority_encoder_4 (
    .in0(1'b1), .in1(and_2_out), .in2(and_3_out), .out(priority_encoder_4_out));  // open: in3, gs, en_out, en_in
  Priority_Encoder #(.select(2)) priority_encoder_5 (
    .in0(1'b1), .in1(decoder_1_out4), .in2(decoder_1_out5), .out(DMwrstate));  // open: in3, gs, en_out, en_in
  Multiplexer #(.enable("false")) multiplexer_1 (.in0(and_5_out), .in1(not_2_out), .out(GRFwen), .sel(or_2_out));
  not not_2 (not_2_out, and_5_out);
  Multiplexer #(.width(2), .enable("false")) multiplexer_2 (
    .in0(priority_encoder_4_out), .in1(2'b11), .out(PCsrc), .sel(and_4_out));

  // Notes on the sheet:
  //   Store
  //   Load
  //   Imm
  //   J&B
  //   R-type
  //   Bran
  //   Jmp
  //   R,J,B
  //   Imm
  //   special for JR & JAL
  //   JR
  //   Load
  //   Store
endmodule
